# Fritzing sketch fritzing (saved by Fritzing 0.9.3b)
circuit board: 8.11083cm x 6.12838cm

parts:
  U1 = ESP32S-HiLetgo [part_number=ESP32S-HiLetgo]
  R1 = Resistor [tolerance=±5% resistance=470 package=THT]
  R2 = Resistor [tolerance=±5% resistance=470 package=THT]
  Q2 = NPN-Transistor [package="TO92 [THT]"]
  LED1 = LED - 5mm [color="Infrared (850nm)" package="5 mm [THT]"]
  LED2 = smd LED [color="Red (633nm)" package="1206 [SMD]"]
  S1 = Pushbutton [package=THT]
  S2 = Pushbutton [package=THT]
  S3 = Pushbutton [package=THT]
  S4 = Pushbutton [package=THT]
  J2 = female pin header, 4 pins [form="♀ (female)"]
  Power_plug2 = Power plug
  Q1 = NPN-Transistor [package="TO92 [THT]"]
  DRV_1 = DRV 8825 Stepper Motor Carrier, High Current [part_number="DRV 8825"]
  U2 = Voltage Regulator - 3.3V [package="TO220 [THT]"]
  R5 = Resistor [tolerance=±5% resistance=10k package=THT]
  R3 = Resistor [tolerance=±5% resistance=10k package=THT]
  R6 = Resistor [tolerance=±5% resistance=10k package=THT]
  R4 = Resistor [tolerance=±5% resistance=10k package=THT]
  C2 = Electrolytic Capacitor [capacitance=100µF voltage=16V package="100 mil [THT, electrolytic]"]

nets (from the breadboard view):
  N1: U1.3.3, LED1.anode, LED2.anode, S1.leg0, S2.leg0, S3.leg0, S4.leg0, U2.output_voltage
  N2: U1.GPIO25, DRV_1.DIRECTION
  N3: U1.GPIO26, DRV_1.STEP
  N4: U1.GPIO27, DRV_1.SLEEP
  N5: U1.GPIO14, DRV_1.RESET
  N6: U1.GPIO12, DRV_1.MS3
  GND: U1.GND, Q2.E, Power_plug2.GND, Q1.E, DRV_1.MS2, DRV_1.GROUND_ST/_MT, DRV_1.GROUND_LOG, U2.GND, R5.Pin_0, R3.Pin_0, R6.Pin_0, R4.Pin_0, C2.-
  N7: U1.GPIO13, DRV_1.MS1
  N8: U1.GPIO9, DRV_1.ENABLE
  N9: U1.GPIO15, R2.Pin_1
  N10: U1.GPIO2, R1.Pin_1
  N11: U1.GPIO4, S1.leg1, R3.Pin_1
  N12: U1.GPIO16, S2.leg1, R4.Pin_1
  N13: U1.GPIO17, S3.leg1, R5.Pin_1
  N14: U1.GPIO5, S4.leg1, R6.Pin_1
  N15: R1.Pin_0, Q2.B
  N16: R2.Pin_0, Q1.B
  N17: Q2.C, LED2.cathode
  N18: LED1.cathode, Q1.C
  N19: J2.pin1, DRV_1.OUT_2B
  N20: J2.pin2, DRV_1.OUT_2A
  N21: J2.pin3, DRV_1.OUT_1A
  N22: J2.pin4, DRV_1.OUT_1B
  N23: Power_plug2.VCC, DRV_1.VOLTAGE_ST/_MT, U2.input_voltage, C2.+

custom parts:
  ESP32S-HiLetgo: HiLetgo ESP-WROOM-32 ESP32 ESP-32S Development Board 2.4GHz Dual-Mode WiFi + Bluetooth Dual Cores Microcontroller The ESP32 integrated with Antenna switches, RF Balun, power amplifiers, low-noise amplifiers, filters, and management modules, and the entire solution occupies the least area of PCB. 2.4 GHz Wi-Fi plus Bluetooth dual-mode chip, with TSMC Ultra-low power consumption 40nm technology,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
