# Fritzing sketch fritzing_2 (saved by Fritzing 0.9.3b)
perfboards: 1

parts:
  LED1 = LED - 5mm [color="Infrared (850nm)" package="5 mm [THT]"]
  Q1 = NPN-Transistor [package="TO92 [THT]"]
  U1 = ESP32S-HiLetgo [part_number=ESP32S-HiLetgo]
  Q2 = NPN-Transistor [package="TO92 [THT]"]
  R3 = Resistor [tolerance=±5% resistance=10k package=THT]
  R4 = Resistor [tolerance=±5% resistance=10k package=THT]
  U2 = Voltage Regulator - 3.3V [package="TO220 [THT]"]
  C2 = Electrolytic Capacitor [capacitance=100µF voltage=16V package="100 mil [THT, electrolytic]"]
  R5 = Resistor [tolerance=±5% resistance=10k package=THT]
  R6 = Resistor [tolerance=±5% resistance=10k package=THT]
  R1 = Resistor [tolerance=±5% resistance=470 package=THT]
  Power_plug2 = Power plug
  DRV_2 = DRV 8825 Stepper Motor Carrier, High Current [part_number="DRV 8825"]
  S5 = Momentary Switch [package=ksa_sealed_tac_switch]
  S6 = Momentary Switch [package=ksa_sealed_tac_switch]
  S7 = Momentary Switch [package=ksa_sealed_tac_switch]
  S8 = Momentary Switch [package=ksa_sealed_tac_switch]
  J3 = screw terminal, 7 pins
  J4 = female pin header, 4 pins [form="♀ (female)"]
  J5 = female pin header, 8 pins [form="♀ (female)"]
  J6 = male pin header, 3 pins [form="♂ (male)"]
  R2 = Resistor [tolerance=±5% resistance=470 package=THT]
  J7 = female pin header, 2 pins [form="♀ (female)"]
  LED2 = LED - 3mm [color="Red (633nm)" package="3 mm [THT]"]

nets:
  N1: LED1.cathode, J6.pin3
  N2: LED1.anode, S5.3, S6.3, S7.3, J7.pin2
  GND: Q1.E, U1.GND, Q2.E, R3.Pin_0, R4.Pin_0, U2.GND, C2.-, R5.Pin_0, R6.Pin_0, Power_plug2.GND, DRV_2.ENABLE, DRV_2.GROUND_ST/_MT, DRV_2.GROUND_LOG
  N3: Q1.B, R2.Pin_0
  N4: Q1.C, J6.pin2
  N5: U1.3.3, U2.output_voltage, LED2.anode
  N6: U1.GPIO32, DRV_2.DIRECTION
  N7: U1.GPIO33, DRV_2.STEP
  N8: U1.GPIO25, DRV_2.SLEEP
  N9: U1.GPIO26, DRV_2.RESET
  N10: U1.GPIO27, DRV_2.MS3
  N11: U1.GPIO14, DRV_2.MS2
  N12: U1.GPIO12, DRV_2.MS1
  N13: U1.GPIO15, R2.Pin_1
  N14: U1.GPIO2, R1.Pin_1
  N15: U1.GPIO4, R3.Pin_1, S8.2, J5.pin8
  N16: U1.GPIO16, R4.Pin_1, S7.2, J5.pin6
  N17: U1.GPIO17, R5.Pin_1, S6.2, J5.pin4
  N18: U1.GPIO5, R6.Pin_1, S5.2, J5.pin2
  N19: Q2.B, R1.Pin_0
  N20: Q2.C, LED2.cathode
  12V: U2.input_voltage, C2.+, Power_plug2.VCC, DRV_2.VOLTAGE_ST/_MT
  N21: DRV_2.OUT_2B, J3.pin1, J4.pin4
  N22: DRV_2.OUT_2A, J3.pin3, J4.pin3
  N23: DRV_2.OUT_1A, J3.pin5, J4.pin2
  N24: DRV_2.OUT_1B, J3.pin7, J4.pin1
  N25: S5.4, J5.pin1
  N26: S6.4, J5.pin3
  N27: S7.4, J5.pin5
  N28: S8.4, J5.pin7
  N29: J6.pin1, J7.pin1

custom parts:
  ESP32S-HiLetgo: HiLetgo ESP-WROOM-32 ESP32 ESP-32S Development Board 2.4GHz Dual-Mode WiFi + Bluetooth Dual Cores Microcontroller The ESP32 integrated with Antenna switches, RF Balun, power amplifiers, low-noise amplifiers, filters, and management modules, and the entire solution occupies the least area of PCB. 2.4 GHz Wi-Fi plus Bluetooth dual-mode chip, with TSMC Ultra-low power consumption 40nm technology,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
  DRV 8825 Stepper Motor Carrier, High Current: This is a Stepper Motor Controller for integrated circuits. This breakout board for TI’s DRV8825 microstepping bipolar stepper motor driver features adjustable current limiting, over-current and over-temperature protection, and six microstep resolutions (down to 1/32-step). It operates from 8.2 V to 45 V and can deliver up to approximately 1.5 A per phase without a heat sink or forced air flow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
